# Fritzing sketch sistema temperatura (saved by Fritzing 0.7.11b)
breadboards: 1

parts:
  R1 = Resistor [tolerance=±5% resistance=10k package=THT]
  Arduino1 = Arduino
  U1 = mystery part, 2 pins [chip_label=termoresistore]

nets:
  N1: R1.Pin_0, U1.pin2
  N2: R1.Pin_1, Arduino1.+5V, Arduino1.A0
  N3: Arduino1.GND, U1.pin1
